// Logisim project control-logic.circ as structural Verilog: 1 circuit, main circuit control_logic
module control_logic (
  input  [31:0] Instruction,
  input  BrEq,
  input  BrLt,
  output PCSel,
  output RegWEn,
  output [2:0] ImmSel,
  output BrUn,
  output ASel,
  output BSel,
  output [3:0] ALUSel,
  output MemWEn,
  output [1:0] WBSel
);

  wire ALU, and_5_out, and_6_out, and_7_out, and_8_out, and_9_out, and_10_out, comparator_1_eq,
       comparator_2_eq, comparator_3_eq, comparator_4_eq, comparator_5_eq, comparator_6_eq, comparator_7_eq,
       comparator_8_eq, comparator_9_eq, comparator_10_eq, comparator_11_eq, comparator_12_eq,
       comparator_13_eq, comparator_14_eq, comparator_15_eq, comparator_16_eq, comparator_17_eq,
       comparator_18_eq, comparator_19_eq, comparator_20_eq, comparator_21_eq, comparator_22_eq,
       comparator_23_eq, comparator_24_eq, comparator_25_eq, comparator_26_eq, comparator_27_eq,
       comparator_28_eq, comparator_29_eq, comparator_31_eq, comparator_32_eq, comparator_33_eq,
       comparator_34_eq, comparator_35_eq, comparator_36_eq, comparator_37_eq, comparator_38_eq,
       comparator_39_eq, comparator_40_eq, comparator_41_eq, comparator_42_eq, comparator_43_eq,
       comparator_44_eq, comparator_45_eq, comparator_46_eq, comparator_47_eq, comparator_48_eq,
       comparator_51_eq, comparator_52_eq, comparator_54_eq, comparator_55_eq, comparator_56_eq,
       comparator_57_eq, comparator_58_eq, comparator_59_eq, comparator_60_eq, comparator_62_eq, ImmB, ImmJ,
       ImmS, ImmU, lui, mul, mulh, not_1_out, not_2_out, not_3_out, or_1_out, or_2_out, or_3_out, or_10_out,
       or_11_out, or_12_out, PCcounter, sra1, sub;
  wire [1:0] multiplexer_8_out;
  wire [2:0] multiplexer_10_out, multiplexer_11_out, multiplexer_12_out;
  wire [3:0] aluSel_t, multiplexer_1_out, multiplexer_2_out, multiplexer_3_out, multiplexer_4_out,
       multiplexer_6_out;
  wire [15:0] rom_1_data;

  Comparator #(.width(7)) comparator_1 (.a(Instruction[31:25]), .b(7'b0000001), .eq(comparator_1_eq));  // open: gt, lt
  and and_1 (mul, comparator_1_eq, comparator_2_eq, comparator_3_eq);
  Comparator #(.width(3)) comparator_2 (.a(Instruction[14:12]), .b(3'b000), .eq(comparator_2_eq));  // open: gt, lt
  Comparator #(.width(7)) comparator_3 (.a(Instruction[6:0]), .b(7'b0110011), .eq(comparator_3_eq));  // open: gt, lt
  Comparator #(.width(7)) comparator_4 (.a(Instruction[31:25]), .b(7'b0000001), .eq(comparator_4_eq));  // open: gt, lt
  and and_2 (mulh, comparator_4_eq, comparator_5_eq, comparator_6_eq);
  Comparator #(.width(3)) comparator_5 (.a(Instruction[14:12]), .b(3'b001), .eq(comparator_5_eq));  // open: gt, lt
  Comparator #(.width(7)) comparator_6 (.a(Instruction[6:0]), .b(7'b0110011), .eq(comparator_6_eq));  // open: gt, lt
  Comparator #(.width(7)) comparator_7 (.a(Instruction[31:25]), .b(7'b0100000), .eq(comparator_7_eq));  // open: gt, lt
  and and_3 (sub, comparator_7_eq, comparator_8_eq, comparator_9_eq);
  Comparator #(.width(3)) comparator_8 (.a(Instruction[14:12]), .b(3'b000), .eq(comparator_8_eq));  // open: gt, lt
  Comparator #(.width(7)) comparator_9 (.a(Instruction[6:0]), .b(7'b0110011), .eq(comparator_9_eq));  // open: gt, lt
  Comparator #(.width(7)) comparator_10 (
    .a(Instruction[31:25]), .b(7'b0100000), .eq(comparator_10_eq));  // open: gt, lt
  Comparator #(.width(3)) comparator_11 (.a(Instruction[14:12]), .b(3'b101), .eq(comparator_11_eq));  // open: gt, lt
  Multiplexer #(.select(3), .width(4)) multiplexer_1 (
    .in0(4'b0000), .in1(4'b0001), .in2(4'b0010), .in3(4'b1011), .in4(4'b0100), .in5(4'b0101), .in6(4'b0110),
    .in7(4'b0111), .out(multiplexer_1_out), .sel(Instruction[14:12]));
  Comparator #(.width(7)) comparator_12 (.a(Instruction[6:0]), .b(7'b0110011), .eq(comparator_12_eq));  // open: gt, lt
  Comparator #(.width(7)) comparator_13 (.a(Instruction[6:0]), .b(7'b0010011), .eq(comparator_13_eq));  // open: gt, lt
  Comparator #(.width(7)) comparator_14 (.a(Instruction[6:0]), .b(7'b0110111), .eq(comparator_14_eq));  // open: gt, lt
  Comparator #(.width(7)) comparator_15 (.a(Instruction[6:0]), .b(7'b0010011), .eq(comparator_15_eq));  // open: gt, lt
  Comparator #(.width(7)) comparator_16 (.a(Instruction[6:0]), .b(7'b0110011), .eq(comparator_16_eq));  // open: gt, lt
  Comparator #(.width(7)) comparator_17 (.a(Instruction[6:0]), .b(7'b0000011), .eq(comparator_17_eq));  // open: gt, lt
  Comparator #(.width(7)) comparator_18 (.a(Instruction[6:0]), .b(7'b1100111), .eq(comparator_18_eq));  // open: gt, lt
  Comparator #(.width(7)) comparator_19 (.a(Instruction[6:0]), .b(7'b1101111), .eq(comparator_19_eq));  // open: gt, lt
  Comparator #(.width(7)) comparator_20 (.a(Instruction[6:0]), .b(7'b0110111), .eq(comparator_20_eq));  // open: gt, lt
  Comparator #(.width(7)) comparator_21 (.a(Instruction[6:0]), .b(7'b0010111), .eq(comparator_21_eq));  // open: gt, lt
  Comparator #(.width(7)) comparator_22 (.a(Instruction[6:0]), .b(7'b0010011), .eq(comparator_22_eq));  // open: gt, lt
  Comparator #(.width(7)) comparator_23 (.a(Instruction[6:0]), .b(7'b1100011), .eq(comparator_23_eq));  // open: gt, lt
  Comparator #(.width(7)) comparator_24 (.a(Instruction[6:0]), .b(7'b0000011), .eq(comparator_24_eq));  // open: gt, lt
  Comparator #(.width(7)) comparator_25 (.a(Instruction[6:0]), .b(7'b0100011), .eq(comparator_25_eq));  // open: gt, lt
  Comparator #(.width(7)) comparator_26 (.a(Instruction[6:0]), .b(7'b1101111), .eq(comparator_26_eq));  // open: gt, lt
  Comparator #(.width(7)) comparator_27 (.a(Instruction[6:0]), .b(7'b1100111), .eq(comparator_27_eq));  // open: gt, lt
  Comparator #(.width(7)) comparator_28 (.a(Instruction[6:0]), .b(7'b0010111), .eq(comparator_28_eq));  // open: gt, lt
  Comparator #(.width(7)) comparator_29 (.a(Instruction[6:0]), .b(7'b0110111), .eq(comparator_29_eq));  // open: gt, lt
  ROM #(.addrWidth(6), .dataWidth(16)) rom_1 (.data(rom_1_data));  // open: addr
  and and_4 (sra1, comparator_10_eq, comparator_11_eq);
  Multiplexer #(.width(4)) multiplexer_2 (.in0(multiplexer_1_out), .in1(4'b1000), .out(multiplexer_2_out), .sel(mul));
  Multiplexer #(.width(4)) multiplexer_3 (.in0(multiplexer_2_out), .in1(4'b1001), .out(multiplexer_3_out), .sel(mulh));
  or or_1 (or_1_out, comparator_12_eq, comparator_13_eq, comparator_14_eq);
  Multiplexer #(.width(4)) multiplexer_4 (.in0(multiplexer_3_out), .in1(4'b1100), .out(multiplexer_4_out), .sel(sub));
  Multiplexer #(.width(4)) multiplexer_5 (.in0(4'b0000), .in1(aluSel_t), .out(ALUSel), .sel(or_1_out));
  or or_2 (or_2_out, comparator_15_eq, comparator_16_eq, comparator_17_eq);
  or or_3 (or_3_out, comparator_19_eq, comparator_20_eq, comparator_21_eq);
  Comparator #(.width(7)) comparator_30 (.a(Instruction[6:0]), .b(7'b0110111), .eq(lui));  // open: gt, lt
  Multiplexer #(.width(4)) multiplexer_6 (.in0(multiplexer_4_out), .in1(4'b1101), .out(multiplexer_6_out), .sel(sra1));
  or or_4 (BSel, comparator_22_eq, comparator_23_eq, comparator_24_eq, comparator_25_eq, comparator_26_eq, comparator_27_eq, comparator_28_eq, comparator_29_eq);
  Multiplexer #(.width(4)) multiplexer_7 (.in0(multiplexer_6_out), .in1(4'b1111), .out(aluSel_t), .sel(lui));
  or or_5 (RegWEn, or_2_out, comparator_18_eq, or_3_out);
  Multiplexer #(.width(2)) multiplexer_8 (.in0(2'b00), .in1(2'b01), .out(multiplexer_8_out), .sel(ALU));
  Comparator #(.width(7)) comparator_31 (.a(Instruction[6:0]), .b(7'b0110011), .eq(comparator_31_eq));  // open: gt, lt
  Comparator #(.width(7)) comparator_32 (.a(Instruction[6:0]), .b(7'b0010111), .eq(comparator_32_eq));  // open: gt, lt
  Comparator #(.width(7)) comparator_33 (.a(Instruction[6:0]), .b(7'b0010011), .eq(comparator_33_eq));  // open: gt, lt
  Comparator #(.width(7)) comparator_34 (.a(Instruction[6:0]), .b(7'b0110111), .eq(comparator_34_eq));  // open: gt, lt
  Comparator #(.width(7)) comparator_35 (.a(Instruction[6:0]), .b(7'b1101111), .eq(comparator_35_eq));  // open: gt, lt
  Comparator #(.width(7)) comparator_36 (.a(Instruction[6:0]), .b(7'b1100111), .eq(comparator_36_eq));  // open: gt, lt
  Multiplexer #(.width(2)) multiplexer_9 (.in0(multiplexer_8_out), .in1(2'b10), .out(WBSel), .sel(PCcounter));
  or or_6 (ALU, comparator_31_eq, comparator_32_eq, comparator_33_eq, comparator_34_eq);
  or or_7 (PCcounter, comparator_35_eq, comparator_36_eq);
  Multiplexer #(.width(3)) multiplexer_10 (.in0(3'b000), .in1(3'b001), .out(multiplexer_10_out), .sel(ImmS));
  Multiplexer #(.width(3)) multiplexer_11 (
    .in0(multiplexer_10_out), .in1(3'b010), .out(multiplexer_11_out), .sel(ImmB));
  Comparator #(.width(7)) comparator_37 (.a(Instruction[6:0]), .b(7'b1100011), .eq(comparator_37_eq));  // open: gt, lt
  Comparator #(.width(3)) comparator_38 (.a(Instruction[14:12]), .b(3'b000), .eq(comparator_38_eq));  // open: gt, lt
  Comparator #(.width(7)) comparator_39 (.a(Instruction[6:0]), .b(7'b1100011), .eq(comparator_39_eq));  // open: gt, lt
  Comparator #(.width(3)) comparator_40 (.a(Instruction[14:12]), .b(3'b101), .eq(comparator_40_eq));  // open: gt, lt
  not not_1 (not_1_out, BrLt);
  Comparator #(.width(7)) comparator_41 (.a(Instruction[6:0]), .b(7'b1100011), .eq(comparator_41_eq));  // open: gt, lt
  Comparator #(.width(3)) comparator_42 (.a(Instruction[14:12]), .b(3'b111), .eq(comparator_42_eq));  // open: gt, lt
  Comparator #(.width(7)) comparator_43 (.a(Instruction[6:0]), .b(7'b1100011), .eq(comparator_43_eq));  // open: gt, lt
  Comparator #(.width(3)) comparator_44 (.a(Instruction[14:12]), .b(3'b100), .eq(comparator_44_eq));  // open: gt, lt
  Comparator #(.width(7)) comparator_45 (.a(Instruction[6:0]), .b(7'b1100011), .eq(comparator_45_eq));  // open: gt, lt
  Comparator #(.width(3)) comparator_46 (.a(Instruction[14:12]), .b(3'b110), .eq(comparator_46_eq));  // open: gt, lt
  Comparator #(.width(7)) comparator_47 (.a(Instruction[6:0]), .b(7'b1100011), .eq(comparator_47_eq));  // open: gt, lt
  Comparator #(.width(3)) comparator_48 (.a(Instruction[14:12]), .b(3'b001), .eq(comparator_48_eq));  // open: gt, lt
  Multiplexer #(.width(3)) multiplexer_12 (
    .in0(multiplexer_11_out), .in1(3'b011), .out(multiplexer_12_out), .sel(ImmU));
  Comparator #(.width(7)) comparator_49 (.a(Instruction[6:0]), .b(7'b0100011), .eq(ImmS));  // open: gt, lt
  Comparator #(.width(7)) comparator_50 (.a(Instruction[6:0]), .b(7'b1100011), .eq(ImmB));  // open: gt, lt
  Comparator #(.width(7)) comparator_51 (.a(Instruction[6:0]), .b(7'b0010111), .eq(comparator_51_eq));  // open: gt, lt
  Comparator #(.width(7)) comparator_52 (.a(Instruction[6:0]), .b(7'b0110111), .eq(comparator_52_eq));  // open: gt, lt
  Comparator #(.width(7)) comparator_53 (.a(Instruction[6:0]), .b(7'b1101111), .eq(ImmJ));  // open: gt, lt
  Comparator #(.width(7)) comparator_54 (.a(Instruction[6:0]), .b(7'b1100011), .eq(comparator_54_eq));  // open: gt, lt
  Comparator #(.width(7)) comparator_55 (.a(Instruction[6:0]), .b(7'b0010111), .eq(comparator_55_eq));  // open: gt, lt
  Comparator #(.width(7)) comparator_56 (.a(Instruction[6:0]), .b(7'b1101111), .eq(comparator_56_eq));  // open: gt, lt
  not not_2 (not_2_out, BrLt);
  not not_3 (not_3_out, BrEq);
  or or_8 (ASel, comparator_54_eq, comparator_55_eq, comparator_56_eq);
  Multiplexer #(.width(3)) multiplexer_13 (.in0(multiplexer_12_out), .in1(3'b100), .out(ImmSel), .sel(ImmJ));
  or or_9 (ImmU, comparator_51_eq, comparator_52_eq);
  and and_5 (and_5_out, comparator_37_eq, comparator_38_eq, BrEq);
  and and_6 (and_6_out, comparator_39_eq, comparator_40_eq, not_1_out);
  and and_7 (and_7_out, comparator_41_eq, comparator_42_eq, not_2_out);
  and and_8 (and_8_out, comparator_43_eq, comparator_44_eq, BrLt);
  and and_9 (and_9_out, comparator_45_eq, comparator_46_eq, BrLt);
  Comparator #(.width(7)) comparator_57 (.a(Instruction[6:0]), .b(7'b1101111), .eq(comparator_57_eq));  // open: gt, lt
  Comparator #(.width(7)) comparator_58 (.a(Instruction[6:0]), .b(7'b1100111), .eq(comparator_58_eq));  // open: gt, lt
  and and_10 (and_10_out, comparator_47_eq, comparator_48_eq, not_3_out);
  or or_10 (or_10_out, comparator_57_eq, comparator_58_eq);
  Comparator #(.width(3)) comparator_59 (.a(Instruction[14:12]), .b(3'b110), .eq(comparator_59_eq));  // open: gt, lt
  Comparator #(.width(3)) comparator_60 (.a(Instruction[14:12]), .b(3'b111), .eq(comparator_60_eq));  // open: gt, lt
  or or_11 (or_11_out, and_5_out, and_6_out, and_7_out, and_8_out, and_9_out, and_10_out);
  Comparator #(.width(7)) comparator_61 (.a(Instruction[6:0]), .b(7'b0100011), .eq(MemWEn));  // open: gt, lt
  Comparator #(.width(7)) comparator_62 (.a(Instruction[6:0]), .b(7'b1100011), .eq(comparator_62_eq));  // open: gt, lt
  or or_12 (or_12_out, comparator_59_eq, comparator_60_eq);
  and and_11 (BrUn, comparator_62_eq, or_12_out);
  or or_13 (PCSel, or_10_out, or_11_out);

  // Other names for the same wires on the sheet: opcode[6:0] = Instruction[6:0]; rd[4:0] = Instruction[11:7];
  //   func3[2:0] = Instruction[14:12]; rs1[4:0] = Instruction[19:15]; rs2[4:0] = Instruction[24:20];
  //   func7[6:0] = Instruction[31:25]

  // Notes on the sheet:
  //   INPUTS to your circuit
  //   Decode the 32 bits Instruction to each field
  //   ALU operations specifically in R type
  //   Connect ROM Input here ->
  //   ROM FOR CONTROL LOGIC
  //   Match ALU operations with corresponding func3 code, add multiplexer for mul, mulh, sub, and sra1
  //   B selector, include all types that needs to calculate immediate or offsets
  //   DON'T CHANGE THE LOCATIONS OF THE INPUTS AND OUTPUTS!
  //   This is only if you choose to do the ROM option
  //   CONNECT
  //   WIRE
  //   TO
  //   USE
  //   ROM
  //   OUTPUT from your circuit
  //   Since all other types use ALU to find PC to jump to, so ALU only works as ADD in other types, and only R and I type use ALU for various operations
  //   Reminder: If using ROM, use combinational logic for PCSel
  //   A selector
  //   Immediate selector, select based on opcode
  //   beq
  //   bge
  //   bgeu
  //   blt
  //   bltu
  //   bne
  //   PC selectors, all types that uses PC
endmodule
