// Logisim project imm-gen.circ as structural Verilog: 1 circuit, main circuit imm_gen
module imm_gen (
  input  [31:0] Instruction,
  input  [2:0] ImmSel,
  output [31:0] Immediate
);

  wire [11:0] UType;
  wire [31:0] IStarType, IType, SType;
  wire [31:12] BType;
  wire [31:20] JType;

  assign UType = {{11{1'b0}}, 1'b0};  // Bit_Extender bit_extender_1
  assign IType = {{20{Instruction[31]}}, Instruction[31:20]};  // Bit_Extender bit_extender_2
  assign IStarType = {{27{1'b0}}, Instruction[24:20]};  // Bit_Extender bit_extender_3
  assign SType = {{20{Instruction[31]}}, {Instruction[31:25], Instruction[11:7]}};  // Bit_Extender bit_extender_4
  assign BType = {{19{Instruction[31]}}, Instruction[31]};  // Bit_Extender bit_extender_5
  assign JType = {{11{Instruction[31]}}, Instruction[31]};  // Bit_Extender bit_extender_6
  Multiplexer #(.select(3), .width(32)) multiplexer_1 (
    .in0(IType), .in1(SType), .in2({BType, Instruction[7], Instruction[30:25], Instruction[11:8], 1'b0}),
    .in3({Instruction[31:12], UType}),
    .in4({JType, Instruction[19:12], Instruction[20], Instruction[30:21], 1'b0}), .out(Immediate),
    .sel(ImmSel));  // open: in5, in6, in7

  // Other names for the same wires on the sheet: BType[11:1] = {Instruction[7], Instruction[30:25], Instruction[11:8]};
  //   JType[19:1] = {Instruction[19:12], Instruction[20], Instruction[30:21]}; UType[31:12] = Instruction[31:12]

  // Notes on the sheet:
  //   INPUTS to your circuit
  //   DON'T CHANGE THE LOCATIONS OF THE INPUTS AND OUTPUTS!
  //   OUTPUT from your circuit
endmodule
