// Logisim project partial-store.circ as structural Verilog: 1 circuit, main circuit partial_store
module partial_store (
  input  [31:0] Instruction,
  input  [31:0] MemAddress,
  input  [31:0] DataFromReg,
  input  MemWEn,
  output [3:0] MemWriteMask,
  output [31:0] DataToMem
);

  wire [3:0] multiplexer_1_out, multiplexer_2_out;
  wire [31:0] bit_extender_1_out, bit_extender_2_out, multiplexer_4_out, multiplexer_5_out, shifter_1_out,
       shifter_2_out, shifter_3_out, shifter_4_out;

  Multiplexer #(.select(2), .width(4)) multiplexer_1 (
    .in0(4'b0001), .in1(4'b0011), .in2(4'b1111), .out(multiplexer_1_out), .sel(Instruction[13:12]));  // open: in3
  Multiplexer #(.select(2), .width(4)) multiplexer_2 (
    .in0(4'b0100), .in1(4'b1100), .out(multiplexer_2_out), .sel(Instruction[13:12]));  // open: in2, in3
  assign bit_extender_1_out = {{24{1'b0}}, DataFromReg[7:0]};  // Bit_Extender bit_extender_1
  assign bit_extender_2_out = {{16{1'b0}}, DataFromReg[15:0]};  // Bit_Extender bit_extender_2
  Shifter #(.width(32)) shifter_1 (.in(bit_extender_1_out), .\dist (5'b01000), .out(shifter_1_out));
  Shifter #(.width(32)) shifter_2 (.in(bit_extender_1_out), .\dist (5'b10000), .out(shifter_2_out));
  Shifter #(.width(32)) shifter_3 (.in(bit_extender_1_out), .\dist (5'b11000), .out(shifter_3_out));
  Shifter #(.width(32)) shifter_4 (.in(bit_extender_2_out), .\dist (5'b10000), .out(shifter_4_out));
  Multiplexer #(.enable("true"), .select(2), .width(4)) multiplexer_3 (
    .in0(multiplexer_1_out), .in1(4'b0010), .in2(multiplexer_2_out), .in3(4'b1000), .out(MemWriteMask),
    .sel(MemAddress[1:0]), .en(MemWEn));
  Multiplexer #(.width(32)) multiplexer_4 (
    .in0(bit_extender_2_out), .in1(shifter_4_out), .out(multiplexer_4_out), .sel(MemAddress[1]));
  Multiplexer #(.select(2), .width(32)) multiplexer_5 (
    .in0(bit_extender_1_out), .in1(shifter_1_out), .in2(shifter_2_out), .in3(shifter_3_out),
    .out(multiplexer_5_out), .sel(MemAddress[1:0]));
  Multiplexer #(.enable("true"), .select(2), .width(32)) multiplexer_6 (
    .in0(multiplexer_5_out), .in1(multiplexer_4_out), .in2(DataFromReg), .out(DataToMem),
    .sel(Instruction[13:12]), .en(MemWEn));  // open: in3

  // Other names for the same wires on the sheet: opcode[6:0] = Instruction[6:0]; rd[4:0] = Instruction[11:7];
  //   func3[2:0] = Instruction[14:12]; rs1[4:0] = Instruction[19:15]; rs2[4:0] = Instruction[24:20];
  //   func7[6:0] = Instruction[31:25]

  // Notes on the sheet:
  //   INPUTS to your circuit
  //   Decode the 32 bits Instruction to each field
  //   DON'T CHANGE THE LOCATIONS OF THE INPUTS AND OUTPUTS!
  //   OUTPUT from your circuit
endmodule
