// Logisim project regfile.circ as structural Verilog: 1 circuit, main circuit regfile
module regfile (
  input  [4:0] ReadIndex1,
  input  [4:0] ReadIndex2,
  input  [4:0] WriteIndex,
  input  [31:0] WriteData,
  input  RegWEn,
  input  clk,
  output [31:0] ra,
  output [31:0] sp,
  output [31:0] t0,
  output [31:0] t1,
  output [31:0] t2,
  output [31:0] s0,
  output [31:0] s1,
  output [31:0] a0,
  output [31:0] ReadData1,
  output [31:0] ReadData2
);

  wire clock_1_out, clock_2_out, clock_3_out, clock_4_out, clock_5_out, clock_6_out, clock_7_out,
       clock_8_out, clock_9_out, clock_10_out, clock_11_out, clock_12_out, clock_13_out, clock_14_out,
       clock_15_out, clock_16_out, clock_17_out, clock_18_out, clock_19_out, clock_20_out, clock_21_out,
       clock_22_out, clock_23_out, clock_24_out, clock_25_out, clock_26_out, clock_27_out, clock_28_out,
       clock_29_out, clock_30_out, clock_31_out, W1, W2, W3, W4, W5, W6, W7, W8, W9, W10, W11, W12, W13, W14,
       W15, W16, W17, W18, W19, W20, W21, W22, W23, W24, W25, W26, W27, W28, W29, W30, W31;
  wire [31:0] x3, x4, x11, x12, x13, x14, x15, x16, x17, x18, x19, x20, x21, x22, x23, x24, x25, x26, x27,
       x28, x29, x30, x31;

  Multiplexer #(.select(5), .width(32)) multiplexer_1 (
    .in0({32{1'b0}}), .in1(ra), .in2(sp), .in3(x3), .in4(x4), .in5(t0), .in6(t1), .in7(t2), .in8(s0),
    .in9(s1), .in10(a0), .in11(x11), .in12(x12), .in13(x13), .in14(x14), .in15(x15), .in16(x16), .in17(x17),
    .in18(x18), .in19(x19), .in20(x20), .in21(x21), .in22(x22), .in23(x23), .in24(x24), .in25(x25),
    .in26(x26), .in27(x27), .in28(x28), .in29(x29), .in30(x30), .in31(x31), .out(ReadData1), .sel(ReadIndex1));
  Multiplexer #(.select(5), .width(32)) multiplexer_2 (
    .in0({32{1'b0}}), .in1(ra), .in2(sp), .in3(x3), .in4(x4), .in5(t0), .in6(t1), .in7(t2), .in8(s0),
    .in9(s1), .in10(a0), .in11(x11), .in12(x12), .in13(x13), .in14(x14), .in15(x15), .in16(x16), .in17(x17),
    .in18(x18), .in19(x19), .in20(x20), .in21(x21), .in22(x22), .in23(x23), .in24(x24), .in25(x25),
    .in26(x26), .in27(x27), .in28(x28), .in29(x29), .in30(x30), .in31(x31), .out(ReadData2), .sel(ReadIndex2));
  Clock clock_1 (.out(clock_1_out));
  Register #(.width(32)) register_1 (.D(WriteData), .en(W1), .clk(clock_1_out), .Q(ra));  // open: clr
  Clock clock_2 (.out(clock_2_out));
  Clock clock_3 (.out(clock_3_out));
  Clock clock_4 (.out(clock_4_out));
  Clock clock_5 (.out(clock_5_out));
  Register #(.width(32)) register_2 (.D(WriteData), .en(W3), .clk(clock_2_out), .Q(x3));  // open: clr
  Register #(.width(32)) register_3 (.D(WriteData), .en(W5), .clk(clock_3_out), .Q(t0));  // open: clr
  Register #(.width(32)) register_4 (.D(WriteData), .en(W7), .clk(clock_4_out), .Q(t2));  // open: clr
  Register #(.width(32)) register_5 (.D(WriteData), .en(W9), .clk(clock_5_out), .Q(s1));  // open: clr
  Clock clock_6 (.out(clock_6_out));
  Clock clock_7 (.out(clock_7_out));
  Clock clock_8 (.out(clock_8_out));
  Clock clock_9 (.out(clock_9_out));
  Clock clock_10 (.out(clock_10_out));
  Clock clock_11 (.out(clock_11_out));
  Register #(.width(32)) register_6 (.D(WriteData), .en(W2), .clk(clock_6_out), .Q(sp));  // open: clr
  Register #(.width(32)) register_7 (.D(WriteData), .en(W4), .clk(clock_7_out), .Q(x4));  // open: clr
  Register #(.width(32)) register_8 (.D(WriteData), .en(W31), .clk(clock_11_out), .Q(x31));  // open: clr
  Register #(.width(32)) register_9 (.D(WriteData), .en(W6), .clk(clock_8_out), .Q(t1));  // open: clr
  Register #(.width(32)) register_10 (.D(WriteData), .en(W8), .clk(clock_9_out), .Q(s0));  // open: clr
  Register #(.width(32)) register_11 (.D(WriteData), .en(W10), .clk(clock_10_out), .Q(a0));  // open: clr
  Demultiplexer #(.select(5)) demultiplexer_1 (
    .out1(W1), .out2(W2), .out3(W3), .out4(W4), .out5(W5), .out6(W6), .out7(W7), .out8(W8), .out9(W9),
    .out10(W10), .out11(W11), .out12(W12), .out13(W13), .out14(W14), .out15(W15), .out16(W16), .out17(W17),
    .out18(W18), .out19(W19), .out20(W20), .out21(W21), .out22(W22), .out23(W23), .out24(W24), .out25(W25),
    .out26(W26), .out27(W27), .out28(W28), .out29(W29), .out30(W30), .out31(W31), .in(RegWEn),
    .sel(WriteIndex));  // open: out0
  Clock clock_12 (.out(clock_12_out));
  Clock clock_13 (.out(clock_13_out));
  Clock clock_14 (.out(clock_14_out));
  Clock clock_15 (.out(clock_15_out));
  Clock clock_16 (.out(clock_16_out));
  Register #(.width(32)) register_12 (.D(WriteData), .en(W11), .clk(clock_12_out), .Q(x11));  // open: clr
  Register #(.width(32)) register_13 (.D(WriteData), .en(W15), .clk(clock_13_out), .Q(x15));  // open: clr
  Register #(.width(32)) register_14 (.D(WriteData), .en(W19), .clk(clock_14_out), .Q(x19));  // open: clr
  Register #(.width(32)) register_15 (.D(WriteData), .en(W23), .clk(clock_15_out), .Q(x23));  // open: clr
  Register #(.width(32)) register_16 (.D(WriteData), .en(W27), .clk(clock_16_out), .Q(x27));  // open: clr
  Clock clock_17 (.out(clock_17_out));
  Clock clock_18 (.out(clock_18_out));
  Clock clock_19 (.out(clock_19_out));
  Clock clock_20 (.out(clock_20_out));
  Register #(.width(32)) register_17 (.D(WriteData), .en(W12), .clk(clock_17_out), .Q(x12));  // open: clr
  Clock clock_21 (.out(clock_21_out));
  Register #(.width(32)) register_18 (.D(WriteData), .en(W16), .clk(clock_18_out), .Q(x16));  // open: clr
  Register #(.width(32)) register_19 (.D(WriteData), .en(W20), .clk(clock_19_out), .Q(x20));  // open: clr
  Register #(.width(32)) register_20 (.D(WriteData), .en(W24), .clk(clock_20_out), .Q(x24));  // open: clr
  Register #(.width(32)) register_21 (.D(WriteData), .en(W28), .clk(clock_21_out), .Q(x28));  // open: clr
  Clock clock_22 (.out(clock_22_out));
  Clock clock_23 (.out(clock_23_out));
  Clock clock_24 (.out(clock_24_out));
  Clock clock_25 (.out(clock_25_out));
  Clock clock_26 (.out(clock_26_out));
  Register #(.width(32)) register_22 (.D(WriteData), .en(W13), .clk(clock_22_out), .Q(x13));  // open: clr
  Register #(.width(32)) register_23 (.D(WriteData), .en(W17), .clk(clock_23_out), .Q(x17));  // open: clr
  Register #(.width(32)) register_24 (.D(WriteData), .en(W21), .clk(clock_24_out), .Q(x21));  // open: clr
  Register #(.width(32)) register_25 (.D(WriteData), .en(W25), .clk(clock_25_out), .Q(x25));  // open: clr
  Register #(.width(32)) register_26 (.D(WriteData), .en(W29), .clk(clock_26_out), .Q(x29));  // open: clr
  Clock clock_27 (.out(clock_27_out));
  Clock clock_28 (.out(clock_28_out));
  Clock clock_29 (.out(clock_29_out));
  Clock clock_30 (.out(clock_30_out));
  Clock clock_31 (.out(clock_31_out));
  Register #(.width(32)) register_27 (.D(WriteData), .en(W14), .clk(clock_27_out), .Q(x14));  // open: clr
  Register #(.width(32)) register_28 (.D(WriteData), .en(W18), .clk(clock_28_out), .Q(x18));  // open: clr
  Register #(.width(32)) register_29 (.D(WriteData), .en(W22), .clk(clock_29_out), .Q(x22));  // open: clr
  Register #(.width(32)) register_30 (.D(WriteData), .en(W26), .clk(clock_30_out), .Q(x26));  // open: clr
  Register #(.width(32)) register_31 (.D(WriteData), .en(W30), .clk(clock_31_out), .Q(x30));  // open: clr

  // Other names for the same wires on the sheet: x1[31:0] = ra; x2[31:0] = sp; x5[31:0] = t0; x6[31:0] = t1;
  //   x7[31:0] = t2; x8[31:0] = s0; x9[31:0] = s1; x10[31:0] = a0

  // Notes on the sheet:
  //   INPUTS to your circuit
  //   DON'T CHANGE THE LOCATIONS OF THE INPUTS AND OUTPUTS!
  //   These are DEBUG/TEST outputs from your circuit.
  //   OUTPUTS from your circuit
endmodule
